# Fritzing sketch ambient_monitor (saved by Fritzing 0.9.3b)
breadboards: 1

parts:
  Raspberry_Pi_1 = Raspberry Pi 3 [part_number=RPI-3-V1.2]
  R1 = PHOTOCELL [package=photocell-kit]
  C2 = Electrolytic Capacitor [capacitance=1µF package="1010 [SMD, electrolytic]"]
  DHT1 = DHT11 Humitidy and Temperature Sensor
  PART1 = SparkFun Soil Moisture Sensor [part_number=SEN-13322]

nets:
  3V3: Raspberry_Pi_1.3v3, R1.P$1, DHT1.DATA, PART1.VCC
  N1: Raspberry_Pi_1.GIPO4, R1.P$2, C2.-
  N2: Raspberry_Pi_1.GIPO7, PART1.SIG
  N3: Raspberry_Pi_1.GIPO8, DHT1.VDD
  GND: Raspberry_Pi_1.GND, C2.+, DHT1.NULL, DHT1.GND, PART1.GND

custom parts:
  DHT11 Humitidy and Temperature Sensor: DHT11 Humidity and Temperature Sensor
  SparkFun Soil Moisture Sensor: The SparkFun Soil Moisture Sensor is a simple breakout for measuring the moisture in soil and similar materials.
